// Logisim project 16BIT.circ as structural Verilog: 9 circuits, main circuit main
module main (
  input  in_1
);

  wire alu_1_p4, alu_1_p5, alu_1_p6, alu_1_p7, alu_1_p8, alu_1_p9, clk_1_clock_output, clock_1_out;
  wire [0:0] x_and_y_register_1_data_out;
  wire [7:0] frame_buffer_1_out_9, frame_buffer_1_out_10, frame_buffer_1_out_11, frame_buffer_1_out_12,
       frame_buffer_1_out_13, frame_buffer_1_out_14, frame_buffer_1_out_15, frame_buffer_1_out_16;
  wire [31:0] accumulator_1_always_out, b_register_1_always_out, program_counter_1_always_out,
       pull_resistor_32_node;

  Clock clock_1 (.out(clock_1_out));
  CLK clk_1 (.CLK_IN(clock_1_out), .CLK_ENB(in_1), .CLOCK_OUTPUT(clk_1_clock_output));  // open: MANUAL_TICK, HALT
  LED led_1 (.in(pull_resistor_32_node[31]));
  LED led_2 (.in(pull_resistor_32_node[30]));
  Pull_Resistor pull_resistor_1 (.node(pull_resistor_32_node[31]));
  Pull_Resistor pull_resistor_2 (.node(pull_resistor_32_node[30]));
  LED led_3 (.in(pull_resistor_32_node[29]));
  LED led_4 (.in(pull_resistor_32_node[28]));
  LED led_5 (.in(pull_resistor_32_node[27]));
  LED led_6 (.in(pull_resistor_32_node[26]));
  Pull_Resistor pull_resistor_3 (.node(pull_resistor_32_node[29]));
  Pull_Resistor pull_resistor_4 (.node(pull_resistor_32_node[28]));
  Pull_Resistor pull_resistor_5 (.node(pull_resistor_32_node[27]));
  Pull_Resistor pull_resistor_6 (.node(pull_resistor_32_node[26]));
  LED led_7 (.in(pull_resistor_32_node[25]));
  LED led_8 (.in(pull_resistor_32_node[24]));
  LED led_9 (.in(pull_resistor_32_node[23]));
  LED led_10 (.in(pull_resistor_32_node[22]));
  Pull_Resistor pull_resistor_7 (.node(pull_resistor_32_node[25]));
  Pull_Resistor pull_resistor_8 (.node(pull_resistor_32_node[24]));
  Pull_Resistor pull_resistor_9 (.node(pull_resistor_32_node[23]));
  Pull_Resistor pull_resistor_10 (.node(pull_resistor_32_node[22]));
  LED led_11 (.in(pull_resistor_32_node[21]));
  LED led_12 (.in(pull_resistor_32_node[20]));
  LED led_13 (.in(pull_resistor_32_node[19]));
  LED led_14 (.in(pull_resistor_32_node[18]));
  Pull_Resistor pull_resistor_11 (.node(pull_resistor_32_node[21]));
  Pull_Resistor pull_resistor_12 (.node(pull_resistor_32_node[20]));
  Pull_Resistor pull_resistor_13 (.node(pull_resistor_32_node[19]));
  Pull_Resistor pull_resistor_14 (.node(pull_resistor_32_node[18]));
  LED led_15 (.in(pull_resistor_32_node[15]));
  LED led_16 (.in(pull_resistor_32_node[14]));
  LED led_17 (.in(pull_resistor_32_node[17]));
  LED led_18 (.in(pull_resistor_32_node[16]));
  Pull_Resistor pull_resistor_15 (.node(pull_resistor_32_node[15]));
  Pull_Resistor pull_resistor_16 (.node(pull_resistor_32_node[14]));
  Pull_Resistor pull_resistor_17 (.node(pull_resistor_32_node[17]));
  Pull_Resistor pull_resistor_18 (.node(pull_resistor_32_node[16]));
  LED led_19 (.in(pull_resistor_32_node[13]));
  LED led_20 (.in(pull_resistor_32_node[12]));
  LED led_21 (.in(pull_resistor_32_node[11]));
  LED led_22 (.in(pull_resistor_32_node[10]));
  Pull_Resistor pull_resistor_19 (.node(pull_resistor_32_node[13]));
  Pull_Resistor pull_resistor_20 (.node(pull_resistor_32_node[12]));
  Pull_Resistor pull_resistor_21 (.node(pull_resistor_32_node[11]));
  Pull_Resistor pull_resistor_22 (.node(pull_resistor_32_node[10]));
  LED led_23 (.in(pull_resistor_32_node[9]));
  LED led_24 (.in(pull_resistor_32_node[8]));
  LED led_25 (.in(pull_resistor_32_node[7]));
  LED led_26 (.in(pull_resistor_32_node[6]));
  Pull_Resistor pull_resistor_23 (.node(pull_resistor_32_node[9]));
  Pull_Resistor pull_resistor_24 (.node(pull_resistor_32_node[8]));
  Pull_Resistor pull_resistor_25 (.node(pull_resistor_32_node[7]));
  Pull_Resistor pull_resistor_26 (.node(pull_resistor_32_node[6]));
  LED led_27 (.in(pull_resistor_32_node[5]));
  LED led_28 (.in(pull_resistor_32_node[4]));
  LED led_29 (.in(pull_resistor_32_node[3]));
  LED led_30 (.in(pull_resistor_32_node[2]));
  Pull_Resistor pull_resistor_27 (.node(pull_resistor_32_node[5]));
  Pull_Resistor pull_resistor_28 (.node(pull_resistor_32_node[4]));
  Pull_Resistor pull_resistor_29 (.node(pull_resistor_32_node[3]));
  Pull_Resistor pull_resistor_30 (.node(pull_resistor_32_node[2]));
  LED led_31 (.in(pull_resistor_32_node[1]));
  LED led_32 (.in(pull_resistor_32_node[0]));
  Pull_Resistor pull_resistor_31 (.node(pull_resistor_32_node[1]));
  Pull_Resistor pull_resistor_32 (.node(pull_resistor_32_node[0]));
  LED led_33 (.in(program_counter_1_always_out[31]));
  LED led_34 (.in(program_counter_1_always_out[30]));
  LED led_35 (.in(program_counter_1_always_out[29]));
  LED led_36 (.in(program_counter_1_always_out[28]));
  LED led_37 (.in(program_counter_1_always_out[27]));
  LED led_38 (.in(program_counter_1_always_out[26]));
  LED led_39 (.in(program_counter_1_always_out[25]));
  LED led_40 (.in(program_counter_1_always_out[24]));
  LED led_41 (.in(program_counter_1_always_out[23]));
  LED led_42 (.in(program_counter_1_always_out[22]));
  LED led_43 (.in(program_counter_1_always_out[21]));
  LED led_44 (.in(program_counter_1_always_out[20]));
  LED led_45 (.in(program_counter_1_always_out[19]));
  LED led_46 (.in(program_counter_1_always_out[18]));
  LED led_47 (.in(program_counter_1_always_out[17]));
  LED led_48 (.in(program_counter_1_always_out[16]));
  LED led_49 (.in(program_counter_1_always_out[15]));
  LED led_50 (.in(program_counter_1_always_out[14]));
  LED led_51 (.in(program_counter_1_always_out[13]));
  LED led_52 (.in(program_counter_1_always_out[12]));
  LED led_53 (.in(program_counter_1_always_out[11]));
  LED led_54 (.in(program_counter_1_always_out[10]));
  LED led_55 (.in(program_counter_1_always_out[9]));
  LED led_56 (.in(program_counter_1_always_out[8]));
  LED led_57 (.in(program_counter_1_always_out[7]));
  LED led_58 (.in(program_counter_1_always_out[6]));
  LED led_59 (.in(program_counter_1_always_out[5]));
  TTY tty_1 (.data(pull_resistor_32_node[6:0]), .clk(clk_1_clock_output));  // open: we, clr
  LED led_60 (.in(program_counter_1_always_out[4]));
  LED led_61 (.in(program_counter_1_always_out[3]));
  LED led_62 (.in(program_counter_1_always_out[2]));
  LED led_63 (.in(program_counter_1_always_out[1]));
  PROGRAM_COUNTER program_counter_1 (
    .CLOCK(clk_1_clock_output), .ADDRESS_IN(pull_resistor_32_node),
    .ALWAYS_OUT(program_counter_1_always_out), .ADDRESS_OUT(pull_resistor_32_node));  // open: RESET, JUMP, COUNTER_ENB, COUNTER_OUT
  X_AND_Y_REGISTER x_and_y_register_1 (
    .CLOCK(clk_1_clock_output), .DATA_IN({pull_resistor_32_node[31:1], x_and_y_register_1_data_out[0]}),
    .DATA_OUT({pull_resistor_32_node[31:1], x_and_y_register_1_data_out[0]}));  // open: WRITE_X, WRITE_Y, READ_X, READ_Y, RESET, Y_ALWAYS_OYT, X_ALWAYS_OUT
  LED led_64 (.in(program_counter_1_always_out[0]));
  ACCUMULATOR accumulator_1 (
    .in_1(pull_resistor_32_node), .CLOCK(clk_1_clock_output), .ALWAYS_OUT(accumulator_1_always_out),
    .DATA_OUT(pull_resistor_32_node));  // open: A_READ, RESET, A_WRITE
  B_REGISTER b_register_1 (
    .DATA_IN(pull_resistor_32_node), .CLOCK(clk_1_clock_output), .ALWAYS_OUT(b_register_1_always_out),
    .DATA_OUT(pull_resistor_32_node));  // open: B_WRITE, B_READ, RESET
  // ALU alu_1: pin names not known; wires that end beside it: pull_resistor_32_node, accumulator_1_always_out, b_register_1_always_out, alu_1_p4, alu_1_p5, alu_1_p6, alu_1_p7, alu_1_p8, alu_1_p9
  DotMatrix #(.inputtype("row"), .matrixcols(8), .matrixrows(8)) dotmatrix_1 (
    .row0(frame_buffer_1_out_10), .row1(frame_buffer_1_out_9), .row2(frame_buffer_1_out_11),
    .row3(frame_buffer_1_out_12), .row4(frame_buffer_1_out_13), .row5(frame_buffer_1_out_14),
    .row6(frame_buffer_1_out_15), .row7(frame_buffer_1_out_16));
  FRAME_BUFFER frame_buffer_1 (
    .CLOCK(clk_1_clock_output), .DATA_IN(pull_resistor_32_node[7:0]),
    .ADDRESS_SELECT(pull_resistor_32_node[2:0]), .out_9(frame_buffer_1_out_9),
    .out_10(frame_buffer_1_out_10), .out_11(frame_buffer_1_out_11), .out_12(frame_buffer_1_out_12),
    .out_13(frame_buffer_1_out_13), .out_14(frame_buffer_1_out_14), .out_15(frame_buffer_1_out_15),
    .out_16(frame_buffer_1_out_16));  // open: RESET_BUFFER, UPDATE_DISPLAY, RESET_DISPLAY, BUFFER_ADDRESS_WRITE_ENABLE, DATA_WRITE_ENABLE
  FLAGS_REGISTER flags_register_1 (
    .CARRY(alu_1_p4), .BORROW(alu_1_p5), .GREATER(alu_1_p6), .EQUAL(alu_1_p7), .LESS(alu_1_p8),
    .ZERO(alu_1_p9), .CLOCK(clk_1_clock_output));  // open: MATH_FLAG_SET, COMPARE_FLAG_SET, RESET, CARRY_FLAG, ZERO_FLAG, BORROW_FLAG, GREATER_FLAG, EQUAL_FLAG, LESS_FLAG
endmodule

module CLK (
  input  CLK_IN,
  input  CLK_ENB,
  input  MANUAL_TICK,
  input  HALT,
  output CLOCK_OUTPUT
);

  wire and_1_out, and_2_out, not_1_out, not_2_out, or_1_out;

  not not_1 (not_1_out, CLK_ENB);
  and and_1 (and_1_out, CLK_IN, CLK_ENB);
  and and_2 (and_2_out, not_1_out, MANUAL_TICK);
  or or_1 (or_1_out, and_1_out, and_2_out);
  not not_2 (not_2_out, HALT);
  and and_3 (CLOCK_OUTPUT, or_1_out, not_2_out);
endmodule

module PROGRAM_COUNTER (
  input  RESET,
  input  JUMP,
  input  COUNTER_ENB,
  input  CLOCK,
  input  [31:0] ADDRESS_IN,
  input  COUNTER_OUT,
  output [31:0] ALWAYS_OUT,
  output [31:0] ADDRESS_OUT
);

  Counter #(.max('hffffffff), .width(32)) counter_1 (
    .clr(RESET), .load(JUMP), .up(COUNTER_ENB), .count(COUNTER_ENB), .clk(CLOCK), .D(ADDRESS_IN),
    .Q(ALWAYS_OUT));  // open: carry
  assign ADDRESS_OUT = COUNTER_OUT ? ALWAYS_OUT : 32'bz;  // Controlled_Buffer controlled_buffer_1
endmodule

module ACCUMULATOR (
  input  [31:0] in_1,
  input  A_WRITE,
  input  A_READ,
  input  CLOCK,
  input  RESET,
  output [31:0] ALWAYS_OUT,
  output [31:0] DATA_OUT
);

  Register #(.width(32)) register_1 (.D(in_1), .en(A_WRITE), .clk(CLOCK), .Q(ALWAYS_OUT), .clr(RESET));
  Controlled_Buffer #(.width(32)) controlled_buffer_1 (.in(ALWAYS_OUT), .out(DATA_OUT));  // open: en
endmodule

module ALU (
  input  BORROW_IN,
  input  CARRY_IN,
  input  [31:0] A_IN,
  input  [31:0] B_IN,
  input  ADD,
  input  SUB,
  input  NOT_A,
  input  A_AND_B,
  input  A_OR_B,
  input  A_XOR_B,
  input  A_NAND_B,
  input  A_NOR_B,
  output CARRY_OUT,
  output BORROW_OUT,
  output GREATER,
  output EQUAL,
  output LESS,
  output [31:0] DATA_OUT,
  output ZERO_FLAG
);

  wire and_2_out, and_3_out, and_4_out, and_5_out, and_6_out, and_7_out, and_8_out, and_9_out, and_10_out,
       and_11_out, and_12_out, and_13_out, and_14_out, and_15_out, and_16_out, and_17_out, and_18_out,
       and_19_out, and_20_out, and_21_out, and_22_out, and_23_out, and_24_out, and_25_out, and_26_out,
       and_27_out, and_28_out, and_29_out, and_30_out, and_31_out, not_2_out, not_3_out, not_4_out,
       not_5_out, not_6_out, not_7_out, not_8_out, not_9_out, not_10_out, not_11_out, not_12_out, not_13_out,
       not_14_out, not_15_out, not_16_out, not_17_out, not_18_out, not_19_out, not_20_out, not_21_out,
       not_22_out, not_23_out, not_24_out, not_25_out, not_26_out, not_27_out, not_28_out, not_29_out,
       not_30_out, not_31_out, not_32_out, not_33_out;
  wire [31:0] adder_1_out, and_1_out, nand_1_out, nor_1_out, not_1_out, or_1_out, or_2_out, subtractor_1_out,
       xor_1_out;

  Adder #(.width(32)) adder_1 (.a(A_IN), .b(B_IN), .out(adder_1_out), .cin(CARRY_IN), .cout(CARRY_OUT));
  Subtractor #(.width(32)) subtractor_1 (
    .a(A_IN), .b(B_IN), .out(subtractor_1_out), .bin(BORROW_IN), .bout(BORROW_OUT));
  Comparator #(.width(32)) comparator_1 (.a(A_IN), .b(B_IN), .gt(GREATER), .eq(EQUAL), .lt(LESS));
  assign not_1_out = ~A_IN;  // NOT_Gate not_1, 32 bits wide
  assign and_1_out = A_IN & B_IN;  // AND_Gate and_1, 32 bits wide
  assign or_1_out = A_IN | B_IN;  // OR_Gate or_1, 32 bits wide
  assign xor_1_out = A_IN ^ B_IN;  // XOR_Gate xor_1, 32 bits wide
  assign nand_1_out = ~(A_IN & B_IN);  // NAND_Gate nand_1, 32 bits wide
  assign nor_1_out = ~(A_IN | B_IN);  // NOR_Gate nor_1, 32 bits wide
  assign DATA_OUT = ADD ? adder_1_out : 32'bz;  // Controlled_Buffer controlled_buffer_1
  assign DATA_OUT = SUB ? subtractor_1_out : 32'bz;  // Controlled_Buffer controlled_buffer_2
  assign DATA_OUT = NOT_A ? not_1_out : 32'bz;  // Controlled_Buffer controlled_buffer_3
  assign DATA_OUT = A_AND_B ? and_1_out : 32'bz;  // Controlled_Buffer controlled_buffer_4
  assign DATA_OUT = A_OR_B ? or_1_out : 32'bz;  // Controlled_Buffer controlled_buffer_5
  assign DATA_OUT = A_XOR_B ? xor_1_out : 32'bz;  // Controlled_Buffer controlled_buffer_6
  assign DATA_OUT = A_NAND_B ? nand_1_out : 32'bz;  // Controlled_Buffer controlled_buffer_7
  assign DATA_OUT = A_NOR_B ? nor_1_out : 32'bz;  // Controlled_Buffer controlled_buffer_8
  assign or_2_out = DATA_OUT;  // OR_Gate or_2, 32 bits wide OR_Gate
  not not_2 (not_2_out, or_2_out[0]);
  not not_3 (not_3_out, or_2_out[1]);
  not not_4 (not_4_out, or_2_out[2]);
  not not_5 (not_5_out, or_2_out[3]);
  and and_2 (and_2_out, not_2_out, not_3_out);
  and and_3 (and_3_out, and_2_out, not_4_out);
  and and_4 (and_4_out, and_3_out, not_5_out);
  and and_5 (and_5_out, and_4_out, not_6_out);
  not not_6 (not_6_out, or_2_out[4]);
  not not_7 (not_7_out, or_2_out[5]);
  not not_8 (not_8_out, or_2_out[6]);
  not not_9 (not_9_out, or_2_out[7]);
  and and_6 (and_6_out, and_5_out, not_7_out);
  and and_7 (and_7_out, and_6_out, not_8_out);
  and and_8 (and_8_out, and_7_out, not_9_out);
  and and_9 (and_9_out, and_8_out, not_10_out);
  not not_10 (not_10_out, or_2_out[8]);
  not not_11 (not_11_out, or_2_out[9]);
  not not_12 (not_12_out, or_2_out[10]);
  not not_13 (not_13_out, or_2_out[11]);
  and and_10 (and_10_out, and_9_out, not_11_out);
  and and_11 (and_11_out, and_10_out, not_12_out);
  and and_12 (and_12_out, and_11_out, not_13_out);
  and and_13 (and_13_out, and_12_out, not_14_out);
  not not_14 (not_14_out, or_2_out[12]);
  not not_15 (not_15_out, or_2_out[13]);
  not not_16 (not_16_out, or_2_out[14]);
  not not_17 (not_17_out, or_2_out[15]);
  and and_14 (and_14_out, and_13_out, not_15_out);
  and and_15 (and_15_out, and_14_out, not_16_out);
  and and_16 (and_16_out, and_15_out, not_17_out);
  and and_17 (and_17_out, and_16_out, not_18_out);
  not not_18 (not_18_out, or_2_out[16]);
  not not_19 (not_19_out, or_2_out[17]);
  not not_20 (not_20_out, or_2_out[18]);
  not not_21 (not_21_out, or_2_out[19]);
  and and_18 (and_18_out, and_17_out, not_19_out);
  and and_19 (and_19_out, and_18_out, not_20_out);
  and and_20 (and_20_out, and_19_out, not_21_out);
  and and_21 (and_21_out, and_20_out, not_22_out);
  not not_22 (not_22_out, or_2_out[20]);
  not not_23 (not_23_out, or_2_out[21]);
  not not_24 (not_24_out, or_2_out[22]);
  not not_25 (not_25_out, or_2_out[23]);
  and and_22 (and_22_out, and_21_out, not_23_out);
  and and_23 (and_23_out, and_22_out, not_24_out);
  and and_24 (and_24_out, and_23_out, not_25_out);
  and and_25 (and_25_out, and_24_out, not_26_out);
  not not_26 (not_26_out, or_2_out[24]);
  not not_27 (not_27_out, or_2_out[25]);
  not not_28 (not_28_out, or_2_out[26]);
  not not_29 (not_29_out, or_2_out[27]);
  and and_26 (and_26_out, and_25_out, not_27_out);
  and and_27 (and_27_out, and_26_out, not_28_out);
  and and_28 (and_28_out, and_27_out, not_29_out);
  and and_29 (and_29_out, and_28_out, not_30_out);
  not not_30 (not_30_out, or_2_out[28]);
  not not_31 (not_31_out, or_2_out[29]);
  not not_32 (not_32_out, or_2_out[30]);
  not not_33 (not_33_out, or_2_out[31]);
  and and_30 (and_30_out, and_29_out, not_31_out);
  and and_31 (and_31_out, and_30_out, not_32_out);
  and and_32 (ZERO_FLAG, and_31_out, not_33_out);
  Pull_Resistor pull_resistor_1 (.node(or_2_out[0]));
  Pull_Resistor pull_resistor_2 (.node(or_2_out[1]));
  Pull_Resistor pull_resistor_3 (.node(or_2_out[2]));
  Pull_Resistor pull_resistor_4 (.node(or_2_out[3]));
  Pull_Resistor pull_resistor_5 (.node(or_2_out[4]));
  Pull_Resistor pull_resistor_6 (.node(or_2_out[5]));
  Pull_Resistor pull_resistor_7 (.node(or_2_out[6]));
  Pull_Resistor pull_resistor_8 (.node(or_2_out[7]));
  Pull_Resistor pull_resistor_9 (.node(or_2_out[8]));
  Pull_Resistor pull_resistor_10 (.node(or_2_out[9]));
  Pull_Resistor pull_resistor_11 (.node(or_2_out[10]));
  Pull_Resistor pull_resistor_12 (.node(or_2_out[11]));
  Pull_Resistor pull_resistor_13 (.node(or_2_out[12]));
  Pull_Resistor pull_resistor_14 (.node(or_2_out[13]));
  Pull_Resistor pull_resistor_15 (.node(or_2_out[14]));
  Pull_Resistor pull_resistor_16 (.node(or_2_out[15]));
  Pull_Resistor pull_resistor_17 (.node(or_2_out[16]));
  Pull_Resistor pull_resistor_18 (.node(or_2_out[17]));
  Pull_Resistor pull_resistor_19 (.node(or_2_out[18]));
  Pull_Resistor pull_resistor_20 (.node(or_2_out[19]));
  Pull_Resistor pull_resistor_21 (.node(or_2_out[20]));
  Pull_Resistor pull_resistor_22 (.node(or_2_out[21]));
  Pull_Resistor pull_resistor_23 (.node(or_2_out[22]));
  Pull_Resistor pull_resistor_24 (.node(or_2_out[23]));
  Pull_Resistor pull_resistor_25 (.node(or_2_out[24]));
  Pull_Resistor pull_resistor_26 (.node(or_2_out[25]));
  Pull_Resistor pull_resistor_27 (.node(or_2_out[26]));
  Pull_Resistor pull_resistor_28 (.node(or_2_out[27]));
  Pull_Resistor pull_resistor_29 (.node(or_2_out[28]));
  Pull_Resistor pull_resistor_30 (.node(or_2_out[29]));
  Pull_Resistor pull_resistor_31 (.node(or_2_out[30]));
  Pull_Resistor pull_resistor_32 (.node(or_2_out[31]));
endmodule

module FLAGS_REGISTER (
  input  CARRY,
  input  BORROW,
  input  GREATER,
  input  EQUAL,
  input  LESS,
  input  ZERO,
  input  MATH_FLAG_SET,
  input  COMPARE_FLAG_SET,
  input  CLOCK,
  input  RESET,
  output CARRY_FLAG,
  output BORROW_FLAG,
  output GREATER_FLAG,
  output EQUAL_FLAG,
  output LESS_FLAG,
  output ZERO_FLAG
);

  Register #(.width(1)) register_1 (.D(CARRY), .en(MATH_FLAG_SET), .clk(CLOCK), .Q(CARRY_FLAG), .clr(RESET));
  Register #(.width(1)) register_2 (.D(BORROW), .en(MATH_FLAG_SET), .clk(CLOCK), .Q(BORROW_FLAG), .clr(RESET));
  Register #(.width(1)) register_3 (.D(GREATER), .en(COMPARE_FLAG_SET), .clk(CLOCK), .Q(GREATER_FLAG), .clr(RESET));
  Register #(.width(1)) register_4 (.D(EQUAL), .en(COMPARE_FLAG_SET), .clk(CLOCK), .Q(EQUAL_FLAG), .clr(RESET));
  Register #(.width(1)) register_5 (.D(LESS), .en(COMPARE_FLAG_SET), .clk(CLOCK), .Q(LESS_FLAG), .clr(RESET));
  Register #(.width(1)) register_6 (.D(ZERO), .en(MATH_FLAG_SET), .clk(CLOCK), .Q(ZERO_FLAG), .clr(RESET));
endmodule

module B_REGISTER (
  input  [31:0] DATA_IN,
  input  B_WRITE,
  input  B_READ,
  input  CLOCK,
  input  RESET,
  output [31:0] ALWAYS_OUT,
  output [31:0] DATA_OUT
);

  Register #(.width(32)) register_1 (.D(DATA_IN), .en(B_WRITE), .clk(CLOCK), .Q(ALWAYS_OUT), .clr(RESET));
  assign DATA_OUT = B_READ ? ALWAYS_OUT : 32'bz;  // Controlled_Buffer controlled_buffer_1
endmodule

module X_AND_Y_REGISTER (
  input  [31:0] DATA_IN,
  input  WRITE_X,
  input  WRITE_Y,
  input  READ_X,
  input  READ_Y,
  input  CLOCK,
  input  RESET,
  output [31:0] X_ALWAYS_OUT,
  output [31:0] DATA_OUT,
  output [31:0] Y_ALWAYS_OYT
);

  Register #(.width(32)) X (.D(DATA_IN), .en(WRITE_X), .clk(CLOCK), .Q(X_ALWAYS_OUT), .clr(RESET));
  Register #(.width(32)) Y (.D(DATA_IN), .en(WRITE_Y), .clk(CLOCK), .Q(Y_ALWAYS_OYT), .clr(RESET));
  assign DATA_OUT = READ_X ? X_ALWAYS_OUT : 32'bz;  // Controlled_Buffer controlled_buffer_1
  assign DATA_OUT = READ_Y ? Y_ALWAYS_OYT : 32'bz;  // Controlled_Buffer controlled_buffer_2
endmodule

module FRAME_BUFFER (
  input  [7:0] DATA_IN,
  input  DATA_WRITE_ENABLE,
  input  [2:0] ADDRESS_SELECT,
  input  BUFFER_ADDRESS_WRITE_ENABLE,
  input  CLOCK,
  input  RESET_BUFFER,
  input  UPDATE_DISPLAY,
  input  RESET_DISPLAY,
  output [7:0] out_9,
  output [7:0] out_10,
  output [7:0] out_11,
  output [7:0] out_12,
  output [7:0] out_13,
  output [7:0] out_14,
  output [7:0] out_15,
  output [7:0] out_16
);

  wire demultiplexer_1_out0, demultiplexer_1_out1, demultiplexer_1_out2, demultiplexer_1_out3,
       demultiplexer_1_out4, demultiplexer_1_out5, demultiplexer_1_out6, demultiplexer_1_out7;
  wire [2:0] register_1_q;
  wire [7:0] register_2_q, register_3_q, register_4_q, register_5_q, register_6_q, register_7_q,
       register_8_q, register_9_q, register_10_q, register_11_q, register_12_q, register_13_q, register_14_q,
       register_15_q, register_16_q, register_17_q, register_18_q, register_19_q, register_20_q,
       register_21_q, register_22_q, register_23_q, register_24_q, register_25_q;

  Register #(.width(3)) register_1 (
    .D(ADDRESS_SELECT), .en(BUFFER_ADDRESS_WRITE_ENABLE), .clk(CLOCK), .Q(register_1_q));  // open: clr
  Demultiplexer #(.select(3)) demultiplexer_1 (
    .out0(demultiplexer_1_out0), .out1(demultiplexer_1_out1), .out2(demultiplexer_1_out2),
    .out3(demultiplexer_1_out3), .out4(demultiplexer_1_out4), .out5(demultiplexer_1_out5),
    .out6(demultiplexer_1_out6), .out7(demultiplexer_1_out7), .in(DATA_WRITE_ENABLE), .sel(register_1_q));
  Register register_2 (.D(DATA_IN), .en(demultiplexer_1_out0), .clk(CLOCK), .Q(register_2_q), .clr(RESET_BUFFER));
  Register register_3 (.D(DATA_IN), .en(demultiplexer_1_out1), .clk(CLOCK), .Q(register_3_q), .clr(RESET_BUFFER));
  Register register_4 (.D(DATA_IN), .en(demultiplexer_1_out2), .clk(CLOCK), .Q(register_4_q), .clr(RESET_BUFFER));
  Register register_5 (.D(DATA_IN), .en(demultiplexer_1_out3), .clk(CLOCK), .Q(register_5_q), .clr(RESET_BUFFER));
  Register register_6 (.D(DATA_IN), .en(demultiplexer_1_out4), .clk(CLOCK), .Q(register_6_q), .clr(RESET_BUFFER));
  Register register_7 (.D(DATA_IN), .en(demultiplexer_1_out5), .clk(CLOCK), .Q(register_7_q), .clr(RESET_BUFFER));
  Register register_8 (.D(DATA_IN), .en(demultiplexer_1_out6), .clk(CLOCK), .Q(register_8_q), .clr(RESET_BUFFER));
  Register register_9 (.D(DATA_IN), .en(demultiplexer_1_out7), .clk(CLOCK), .Q(register_9_q), .clr(RESET_BUFFER));
  Register register_10 (
    .D(register_2_q), .en(demultiplexer_1_out0), .clk(CLOCK), .Q(register_10_q), .clr(RESET_BUFFER));
  Register register_11 (
    .D(register_3_q), .en(demultiplexer_1_out1), .clk(CLOCK), .Q(register_11_q), .clr(RESET_BUFFER));
  Register register_12 (
    .D(register_4_q), .en(demultiplexer_1_out2), .clk(CLOCK), .Q(register_12_q), .clr(RESET_BUFFER));
  Register register_13 (
    .D(register_5_q), .en(demultiplexer_1_out3), .clk(CLOCK), .Q(register_13_q), .clr(RESET_BUFFER));
  Register register_14 (
    .D(register_6_q), .en(demultiplexer_1_out4), .clk(CLOCK), .Q(register_14_q), .clr(RESET_BUFFER));
  Register register_15 (
    .D(register_7_q), .en(demultiplexer_1_out5), .clk(CLOCK), .Q(register_15_q), .clr(RESET_BUFFER));
  Register register_16 (
    .D(register_8_q), .en(demultiplexer_1_out6), .clk(CLOCK), .Q(register_16_q), .clr(RESET_BUFFER));
  Register register_17 (
    .D(register_9_q), .en(demultiplexer_1_out7), .clk(CLOCK), .Q(register_17_q), .clr(RESET_BUFFER));
  Register register_18 (.D(register_10_q), .en(UPDATE_DISPLAY), .clk(CLOCK), .Q(register_18_q), .clr(RESET_DISPLAY));
  Register register_19 (.D(register_11_q), .en(UPDATE_DISPLAY), .clk(CLOCK), .Q(register_19_q), .clr(RESET_DISPLAY));
  Register register_20 (.D(register_12_q), .en(UPDATE_DISPLAY), .clk(CLOCK), .Q(register_20_q), .clr(RESET_DISPLAY));
  Register register_21 (.D(register_13_q), .en(UPDATE_DISPLAY), .clk(CLOCK), .Q(register_21_q), .clr(RESET_DISPLAY));
  Register register_22 (.D(register_14_q), .en(UPDATE_DISPLAY), .clk(CLOCK), .Q(register_22_q), .clr(RESET_DISPLAY));
  Register register_23 (.D(register_15_q), .en(UPDATE_DISPLAY), .clk(CLOCK), .Q(register_23_q), .clr(RESET_DISPLAY));
  Register register_24 (.D(register_16_q), .en(UPDATE_DISPLAY), .clk(CLOCK), .Q(register_24_q), .clr(RESET_DISPLAY));
  Register register_25 (.D(register_17_q), .en(UPDATE_DISPLAY), .clk(CLOCK), .Q(register_25_q), .clr(RESET_DISPLAY));
  Register register_26 (.D(register_18_q), .en(UPDATE_DISPLAY), .clk(CLOCK), .Q(out_9), .clr(RESET_DISPLAY));
  Register register_27 (.D(register_19_q), .en(UPDATE_DISPLAY), .clk(CLOCK), .Q(out_10), .clr(RESET_DISPLAY));
  Register register_28 (.D(register_20_q), .en(UPDATE_DISPLAY), .clk(CLOCK), .Q(out_11), .clr(RESET_DISPLAY));
  Register register_29 (.D(register_21_q), .en(UPDATE_DISPLAY), .clk(CLOCK), .Q(out_12), .clr(RESET_DISPLAY));
  Register register_30 (.D(register_22_q), .en(UPDATE_DISPLAY), .clk(CLOCK), .Q(out_13), .clr(RESET_DISPLAY));
  Register register_31 (.D(register_23_q), .en(UPDATE_DISPLAY), .clk(CLOCK), .Q(out_14), .clr(RESET_DISPLAY));
  Register register_32 (.D(register_24_q), .en(UPDATE_DISPLAY), .clk(CLOCK), .Q(out_15), .clr(RESET_DISPLAY));
  Register register_33 (.D(register_25_q), .en(UPDATE_DISPLAY), .clk(CLOCK), .Q(out_16), .clr(RESET_DISPLAY));
endmodule
